// Logisim project Cpu(Practice).circ as structural Verilog: 9 circuits, main circuit main
module main (
  input  Reset,
  output [31:0] out_2,
  output out_3,
  output [4:0] out_4,
  output [31:0] out_5,
  output out_6,
  output [4:0] out_7,
  output [31:0] out_8
);

  wire alu_1_zero, ALUSrc, and_1_out, clk, DMSrc, nPC_Sel;
  wire [1:0] ALUOp, ExtOp, Jump, MemtoReg, RegDst;
  wire [3:0] alu_control_1_out_3;
  wire [4:0] instructionmemory_1_rd, instructionmemory_1_rs, instructionmemory_1_rt, shamt;
  wire [5:0] Funct, instructionmemory_1_op;
  wire [15:0] instructionmemory_1_imm16;
  wire [25:0] instructionmemory_1_addr26;
  wire [31:0] a, adder_2_out, data_jr, datamemory_1_readdata, ext_1_out_3, MemAddr, multiplexer_2_out,
       multiplexer_3_out, multiplexer_5_out, pc_add_4, shifter_1_out, subtractor_1_out;

  // Probe on out_2
  PC pc_1 (.clk(clk), .reset(Reset), .PC_IN(multiplexer_5_out), .PC_OUT(out_2));
  // Probe on instructionmemory_1_op
  InstructionMemory instructionmemory_1 (
    .address(out_2), .OP(instructionmemory_1_op), .Rs(instructionmemory_1_rs), .Rt(instructionmemory_1_rt),
    .Rd(instructionmemory_1_rd), .Shamt(shamt), .Funct(Funct), .imm16(instructionmemory_1_imm16),
    .addr26(instructionmemory_1_addr26));
  Adder #(.width(32)) adder_1 (.a(32'h4), .b(out_2), .out(pc_add_4));  // open: cin, cout
  Control_Unit control_unit_1 (
    .Op(instructionmemory_1_op), .ExtOp(ExtOp), .ALUOp(ALUOp), .ALUSrc(ALUSrc), .RegWrite(out_3),
    .MemWrite(out_6), .nPC_sel(nPC_Sel), .RegDst(RegDst), .Jump(Jump), .MemtoReg(MemtoReg), .in_2(Funct),
    .DMSrc(DMSrc));
  Multiplexer #(.select(2), .width(5), .enable("false")) multiplexer_1 (
    .in0(instructionmemory_1_rt), .in1(instructionmemory_1_rd), .in2({5{1'b1}}), .out(out_4), .sel(RegDst));  // open: in3
  RegisterFile registerfile_1 (
    .clk(clk), .A1(instructionmemory_1_rs), .A3(out_4), .WD(out_5), .reset(Reset),
    .A2(instructionmemory_1_rt), .WE(out_3), .RD1(data_jr), .RD2(a));
  Ext ext_1 (.ExtOp(ExtOp), .imm16(instructionmemory_1_imm16), .out_3(ext_1_out_3));
  Clock clock_1 (.out(clk));
  // Probe on ALUOp
  Subtractor #(.width(32)) subtractor_1 (
    .a({pc_add_4[31:28], instructionmemory_1_addr26, 2'b00}), .b(32'h3000), .out(subtractor_1_out));  // open: bin, bout
  Shifter #(.width(32)) shifter_1 (.in(ext_1_out_3), .\dist (5'b00010), .out(shifter_1_out));
  Multiplexer #(.width(32), .enable("false")) multiplexer_2 (
    .in0(a), .in1(ext_1_out_3), .out(multiplexer_2_out), .sel(ALUSrc));
  ALU_Control alu_control_1 (.Funct(Funct), .ALU_OP(ALUOp), .out_3(alu_control_1_out_3));
  // Probe on alu_control_1_out_3
  Adder #(.width(32)) adder_2 (.a(pc_add_4), .b(shifter_1_out), .out(adder_2_out));  // open: cin, cout
  and and_1 (and_1_out, nPC_Sel, alu_1_zero);
  ALU alu_1 (
    .A(data_jr), .B(multiplexer_2_out), .Result({MemAddr[31:7], out_7, MemAddr[1:0]}), .Zero(alu_1_zero),
    .OP(alu_control_1_out_3), .shamt(shamt));
  Multiplexer #(.width(32), .enable("false")) multiplexer_3 (
    .in0(pc_add_4), .in1(adder_2_out), .out(multiplexer_3_out), .sel(and_1_out));
  Multiplexer #(.width(32), .enable("false")) multiplexer_4 (
    .in0(a), .in1({a[7:0], a[7:0], a[7:0], a[7:0]}), .out(out_8), .sel(DMSrc));
  Multiplexer #(.select(2), .width(32), .enable("false")) multiplexer_5 (
    .in0(multiplexer_3_out), .in1(subtractor_1_out), .in2(data_jr), .out(multiplexer_5_out), .sel(Jump));  // open: in3
  DataMemory datamemory_1 (
    .Address({MemAddr[31:7], out_7, MemAddr[1:0]}), .WD(out_8), .MemWrite(out_6), .clk(clk), .Reset(Reset),
    .ReadData(datamemory_1_readdata));
  // Probe on MemtoReg
  Multiplexer #(.select(2), .width(32), .enable("false")) multiplexer_6 (
    .in0({MemAddr[31:7], out_7, MemAddr[1:0]}), .in1(datamemory_1_readdata), .in2(pc_add_4), .out(out_5),
    .sel(MemtoReg));  // open: in3

  // Other names for the same wires on the sheet: b[31:0] = {a[7:0], a[7:0], a[7:0], a[7:0]}; Instr[31:0] = out_2;
  //   MemAddr[6:2] = out_7; MemData[31:0] = out_8; MemWrite = out_6; RegAddr[4:0] = out_4; RegData[31:0] = out_5;
  //   RegWrite = out_3
endmodule

// RF
module RegisterFile (
  input  clk,
  input  [4:0] A1,
  input  [4:0] A3,
  input  [31:0] WD,
  input  reset,
  input  [4:0] A2,
  input  WE,
  output [31:0] RD1,
  output [31:0] RD2
);

  wire [31:0] O1, O2, O3, O4, O5, O6, O7, O8, O9, O10, O11, O12, O13, O14, O15, O16, O17, O18, O19, O20, O21,
       O22, O23, O24, O25, O26, O27, O28, O29, O30, O31, O32, REG1, REG2, REG3, REG4, REG5, REG6, REG7, REG8,
       REG9, REG10, REG11, REG12, REG13, REG14, REG15, REG16, REG17, REG18, REG19, REG20, REG21, REG22,
       REG23, REG24, REG25, REG26, REG27, REG28, REG29, REG30, REG31, REG32;

  Register #(.width(32)) register_1 (.D(O1), .en(1'b0), .Q(REG1), .clk(clk), .clr(reset));
  Register #(.width(32)) register_2 (.D(O5), .Q(REG5), .clk(clk), .clr(reset));  // open: en
  Register #(.width(32)) register_3 (.D(O9), .Q(REG9), .clk(clk), .clr(reset));  // open: en
  Register #(.width(32)) register_4 (.D(O13), .Q(REG13), .clk(clk), .clr(reset));  // open: en
  Register #(.width(32)) register_5 (.D(O17), .Q(REG17), .clk(clk), .clr(reset));  // open: en
  Register #(.width(32)) register_6 (.D(O21), .Q(REG21), .clk(clk), .clr(reset));  // open: en
  Register #(.width(32)) register_7 (.D(O25), .Q(REG25), .clk(clk), .clr(reset));  // open: en
  Register #(.width(32)) register_8 (.D(O29), .Q(REG29), .clk(clk), .clr(reset));  // open: en
  Multiplexer #(.select(5), .width(32)) multiplexer_1 (
    .in0(REG1), .in1(REG2), .in2(REG3), .in3(REG4), .in4(REG5), .in5(REG6), .in6(REG7), .in7(REG8),
    .in8(REG9), .in9(REG10), .in10(REG11), .in11(REG12), .in12(REG13), .in13(REG14), .in14(REG15),
    .in15(REG16), .in16(REG17), .in17(REG18), .in18(REG19), .in19(REG20), .in20(REG21), .in21(REG22),
    .in22(REG23), .in23(REG24), .in24(REG25), .in25(REG26), .in26(REG27), .in27(REG28), .in28(REG29),
    .in29(REG30), .in30(REG31), .in31(REG32), .out(RD1), .sel(A1), .en(1'b1));
  Register #(.width(32)) register_9 (.D(O2), .Q(REG2), .clk(clk), .clr(reset));  // open: en
  Register #(.width(32)) register_10 (.D(O6), .Q(REG6), .clk(clk), .clr(reset));  // open: en
  Register #(.width(32)) register_11 (.D(O10), .Q(REG10), .clk(clk), .clr(reset));  // open: en
  Register #(.width(32)) register_12 (.D(O14), .Q(REG14), .clk(clk), .clr(reset));  // open: en
  Register #(.width(32)) register_13 (.D(O18), .Q(REG18), .clk(clk), .clr(reset));  // open: en
  Register #(.width(32)) register_14 (.D(O22), .Q(REG22), .clk(clk), .clr(reset));  // open: en
  Register #(.width(32)) register_15 (.D(O26), .Q(REG26), .clk(clk), .clr(reset));  // open: en
  Register #(.width(32)) register_16 (.D(O30), .Q(REG30), .clk(clk), .clr(reset));  // open: en
  Register #(.width(32)) register_17 (.D(O3), .Q(REG3), .clk(clk), .clr(reset));  // open: en
  Register #(.width(32)) register_18 (.D(O7), .Q(REG7), .clk(clk), .clr(reset));  // open: en
  Register #(.width(32)) register_19 (.D(O11), .Q(REG11), .clk(clk), .clr(reset));  // open: en
  Register #(.width(32)) register_20 (.D(O15), .Q(REG15), .clk(clk), .clr(reset));  // open: en
  Register #(.width(32)) register_21 (.D(O19), .Q(REG19), .clk(clk), .clr(reset));  // open: en
  Register #(.width(32)) register_22 (.D(O23), .Q(REG23), .clk(clk), .clr(reset));  // open: en
  Register #(.width(32)) register_23 (.D(O27), .Q(REG27), .clk(clk), .clr(reset));  // open: en
  Register #(.width(32)) register_24 (.D(O31), .Q(REG31), .clk(clk), .clr(reset));  // open: en
  Multiplexer #(.select(5), .width(32)) multiplexer_2 (
    .in0(REG1), .in1(REG2), .in2(REG3), .in3(REG4), .in4(REG5), .in5(REG6), .in6(REG7), .in7(REG8),
    .in8(REG9), .in9(REG10), .in10(REG11), .in11(REG12), .in12(REG13), .in13(REG14), .in14(REG15),
    .in15(REG16), .in16(REG17), .in17(REG18), .in18(REG19), .in19(REG20), .in20(REG21), .in21(REG22),
    .in22(REG23), .in23(REG24), .in24(REG25), .in25(REG26), .in26(REG27), .in27(REG28), .in28(REG29),
    .in29(REG30), .in30(REG31), .in31(REG32), .out(RD2), .sel(A2), .en(1'b1));
  Register #(.width(32)) register_25 (.D(O4), .Q(REG4), .clk(clk), .clr(reset));  // open: en
  Register #(.width(32)) register_26 (.D(O8), .Q(REG8), .clk(clk), .clr(reset));  // open: en
  Register #(.width(32)) register_27 (.D(O12), .Q(REG12), .clk(clk), .clr(reset));  // open: en
  Register #(.width(32)) register_28 (.D(O16), .Q(REG16), .clk(clk), .clr(reset));  // open: en
  Register #(.width(32)) register_29 (.D(O20), .Q(REG20), .clk(clk), .clr(reset));  // open: en
  Register #(.width(32)) register_30 (.D(O24), .Q(REG24), .clk(clk), .clr(reset));  // open: en
  Register #(.width(32)) register_31 (.D(O28), .Q(REG28), .clk(clk), .clr(reset));  // open: en
  Register #(.width(32)) register_32 (.D(O32), .Q(REG32), .clk(clk), .clr(reset));  // open: en
  Demultiplexer #(.select(5), .width(32), .tristate("true")) demultiplexer_1 (
    .out0(O1), .out1(O2), .out2(O3), .out3(O4), .out4(O5), .out5(O6), .out6(O7), .out7(O8), .out8(O9),
    .out9(O10), .out10(O11), .out11(O12), .out12(O13), .out13(O14), .out14(O15), .out15(O16), .out16(O17),
    .out17(O18), .out18(O19), .out19(O20), .out20(O21), .out21(O22), .out22(O23), .out23(O24), .out24(O25),
    .out25(O26), .out26(O27), .out27(O28), .out28(O29), .out29(O30), .out30(O31), .out31(O32), .in(WD),
    .sel(A3), .en(WE));
endmodule

module PC (
  input  clk,
  input  reset,
  input  [31:0] PC_IN,
  output [31:0] PC_OUT
);

  Register #(.width(32)) register_1 (.D(PC_IN), .Q(PC_OUT), .clk(clk), .clr(reset));  // open: en
endmodule

// IM
module InstructionMemory (
  input  [31:0] address,
  output [5:0] OP,
  output [4:0] Rs,
  output [4:0] Rt,
  output [4:0] Rd,
  output [4:0] Shamt,
  output [15:0] imm16,
  output [5:0] Funct,
  output [25:0] addr26
);

  ROM #(.addrWidth(5), .dataWidth(32)) rom_1 (.addr(address[6:2]), .data({OP, addr26}));  // open: sel
  // Probe on {OP, addr26}

  assign Funct = addr26[5:0];
  assign imm16 = addr26[15:0];
  assign Rd = addr26[15:11];
  assign Rs = addr26[25:21];
  assign Rt = addr26[20:16];
  assign Shamt = addr26[10:6];

  // Notes on the sheet:
  //   contents of rom_1 (hex, n*v repeats v):
  //   34040008 42880 854020 a44822
endmodule

module ALU (
  input  [31:0] A,
  input  [31:0] B,
  input  [3:0] OP,
  input  [4:0] shamt,
  output [31:0] Result,
  output Zero
);

  wire comparator_2_eq;
  wire [4:0] bitfinder_1_index, bitfinder_2_index;
  wire [31:0] adder_1_out, and_1_out, or_1_out, sll_result, ssze_result, subtractor_1_out, subtractor_2_out;

  assign and_1_out = A & B;  // AND_Gate and_1, 32 bits wide
  assign or_1_out = A | B;  // OR_Gate or_1, 32 bits wide
  Adder #(.width(32)) adder_1 (.a(A), .b(B), .out(adder_1_out));  // open: cin, cout
  Subtractor #(.width(32)) subtractor_1 (.a(A), .b(B), .out(subtractor_1_out));  // open: bin, bout
  Multiplexer #(.select(4), .width(32), .enable("false")) multiplexer_1 (
    .in0(and_1_out), .in1(or_1_out), .in2(adder_1_out), .in6(subtractor_1_out), .in14(sll_result),
    .in15(ssze_result), .out(Result), .sel(OP));  // open: in3, in4, in5, in7, in8, in9, in10, in11, in12, in13
  Comparator #(.width(32), .mode("unsigned")) comparator_1 (
    .a(subtractor_1_out), .b({32{1'b0}}), .eq(Zero));  // open: gt, lt
  BitFinder #(.width(32)) bitfinder_1 (.in(A), .index(bitfinder_1_index));  // open: found
  BitFinder #(.width(32)) bitfinder_2 (.in(B), .index(bitfinder_2_index));  // open: found
  Shifter #(.width(32)) shifter_1 (.in(B), .\dist (shamt), .out(sll_result));
  Subtractor #(.width(32)) subtractor_2 (.a(A), .b(B), .out(subtractor_2_out));  // open: bin, bout
  Comparator #(.width(5)) comparator_2 (
    .a(bitfinder_1_index), .b(bitfinder_2_index), .eq(comparator_2_eq));  // open: gt, lt
  Multiplexer #(.width(32), .enable("false")) multiplexer_2 (
    .in0(subtractor_2_out), .in1(32'h1), .out(ssze_result), .sel(comparator_2_eq));
endmodule

module ALU_Control (
  input  [5:0] Funct,
  input  [1:0] ALU_OP,
  output [3:0] out_3
);

  wire _0000_out, _0001_out, _0010_2_out, _0010_out, _0110_2_out, _0110_out, _0111_out, _1110_out, _1111_out,
       not_1_out, not_2_out, not_3_out, not_4_out, not_5_out, not_6_out, not_7_out, not_8_out;

  not not_1 (not_1_out, ALU_OP[1]);
  not not_2 (not_2_out, ALU_OP[0]);
  not not_3 (not_3_out, Funct[5]);
  not not_4 (not_4_out, Funct[3]);
  not not_5 (not_5_out, Funct[4]);
  not not_6 (not_6_out, Funct[2]);
  not not_7 (not_7_out, Funct[1]);
  not not_8 (not_8_out, Funct[0]);
  and _0010 (_0010_out, not_1_out, not_2_out);
  and _0110 (_0110_out, not_1_out, ALU_OP[0]);
  and _0010_2 (_0010_2_out, ALU_OP[1], not_2_out, Funct[5], not_5_out, not_4_out, not_6_out, not_7_out, not_8_out);
  and _0110_2 (_0110_2_out, ALU_OP[1], not_2_out, not_4_out, not_6_out, Funct[1], not_8_out);
  and _0000 (_0000_out, ALU_OP[1], not_2_out, not_4_out, Funct[2], not_7_out, not_8_out);
  and _0001 (_0001_out, ALU_OP[1], ALU_OP[0]);
  and _0111 (_0111_out, ALU_OP[1], not_2_out, Funct[3], not_6_out, Funct[1], not_8_out);
  and _1111 (_1111_out, ALU_OP[1], not_2_out, not_3_out, not_5_out, Funct[3], Funct[2], Funct[1], Funct[0]);
  and _1110 (_1110_out, ALU_OP[1], not_2_out, not_3_out, not_5_out, not_4_out, not_6_out, not_7_out, not_8_out);
  Multiplexer #(.width(4), .enable("false")) multiplexer_1 (.in1(4'b0010), .out(out_3), .sel(_0010_out));  // open: in0
  Multiplexer #(.width(4), .enable("false")) multiplexer_2 (.in1(4'b0110), .out(out_3), .sel(_0110_out));  // open: in0
  Multiplexer #(.width(4), .enable("false")) multiplexer_3 (
    .in1(4'b0010), .out(out_3), .sel(_0010_2_out));  // open: in0
  Multiplexer #(.width(4), .enable("false")) multiplexer_4 (
    .in1(4'b0110), .out(out_3), .sel(_0110_2_out));  // open: in0
  Multiplexer #(.width(4), .enable("false")) multiplexer_5 (.in1(4'b0000), .out(out_3), .sel(_0000_out));  // open: in0
  Multiplexer #(.width(4), .enable("false")) multiplexer_6 (.in1(4'b0001), .out(out_3), .sel(_0001_out));  // open: in0
  Multiplexer #(.width(4), .enable("false")) multiplexer_7 (.in1(4'b0111), .out(out_3), .sel(_0111_out));  // open: in0
  Multiplexer #(.width(4), .enable("false")) multiplexer_8 (.in1(4'b1111), .out(out_3), .sel(_1111_out));  // open: in0
  Multiplexer #(.width(4), .enable("false")) multiplexer_9 (.in1(4'b1110), .out(out_3), .sel(_1110_out));  // open: in0

  // Other names for the same wires on the sheet: ALUOp0 = ALU_OP[0]; ALUOp1 = ALU_OP[1]; F0 = Funct[0]; F1 = Funct[1];
  //   F2 = Funct[2]; F3 = Funct[3]; F4 = Funct[4]; F5 = Funct[5]; Operation[3:0] = out_3
endmodule

// CU
module Control_Unit (
  input  [5:0] Op,
  input  [5:0] in_2,
  output [1:0] ExtOp,
  output [1:0] RegDst,
  output [1:0] MemtoReg,
  output [1:0] ALUOp,
  output [1:0] Jump,
  output ALUSrc,
  output RegWrite,
  output MemWrite,
  output nPC_sel,
  output DMSrc
);

  wire add_out, beq_out, jal_out, jr_out, lui_out, lw_out, memset_out, nop_out, not_1_out, not_2_out,
       not_3_out, not_4_out, not_5_out, not_6_out, not_7_out, not_8_out, not_9_out, not_10_out, not_11_out,
       not_12_out, ori_out, sll_out, ssze_out, sub_out, sw_out;

  not not_1 (not_1_out, Op[5]);
  not not_2 (not_2_out, Op[3]);
  not not_3 (not_3_out, Op[4]);
  not not_4 (not_4_out, Op[2]);
  not not_5 (not_5_out, Op[1]);
  not not_6 (not_6_out, Op[0]);
  not not_7 (not_7_out, in_2[5]);
  not not_8 (not_8_out, in_2[3]);
  not not_9 (not_9_out, in_2[4]);
  not not_10 (not_10_out, in_2[2]);
  not not_11 (not_11_out, in_2[0]);
  not not_12 (not_12_out, in_2[1]);
  and add (add_out, not_1_out, not_3_out, not_2_out, not_4_out, not_5_out, not_6_out);
  and sub (sub_out, not_1_out, not_3_out, not_2_out, not_4_out, not_5_out, not_6_out);
  and ori (ori_out, not_1_out, not_3_out, Op[3], Op[2], not_5_out, Op[0]);
  and lw (lw_out, Op[5], not_3_out, not_2_out, not_4_out, Op[1], Op[0]);
  and sw (sw_out, Op[5], not_3_out, Op[3], not_4_out, Op[1], Op[0]);
  and beq (beq_out, not_1_out, not_3_out, not_2_out, Op[2], not_5_out, not_6_out);
  and lui (lui_out, not_1_out, not_3_out, Op[3], Op[2], Op[1], Op[0]);
  and nop (nop_out, not_1_out, not_3_out, not_2_out, not_4_out, not_5_out, not_6_out);
  and ssze (ssze_out, not_1_out, not_3_out, not_2_out, not_4_out, not_5_out, not_6_out);
  and jal (jal_out, not_1_out, not_3_out, not_2_out, not_4_out, Op[1], Op[0]);
  and jr (jr_out, not_1_out, not_3_out, not_2_out, not_4_out, not_5_out, not_6_out, not_7_out, not_9_out, in_2[3], not_10_out, not_12_out, not_11_out);
  and memset (memset_out, Op[5], Op[4], not_2_out, Op[2], Op[1], not_6_out);
  and sll (sll_out, not_1_out, not_3_out, not_2_out, not_4_out, not_5_out, not_6_out);
  buf RegDst1 (RegDst[1], jal_out);  // OR_Gate
  or RegDst0 (RegDst[0], add_out, sll_out, ssze_out, sub_out);
  or u_ALUSrc (ALUSrc, ori_out, lw_out, memset_out, lui_out, sw_out);
  buf MemtoReg1 (MemtoReg[1], jal_out);  // OR_Gate
  buf MemtoReg0 (MemtoReg[0], lw_out);  // OR_Gate
  or u_RegWrite (RegWrite, jal_out, lui_out, add_out, sub_out, ori_out, lw_out, ssze_out, sll_out);
  or u_MemWrite (MemWrite, sw_out, memset_out);
  buf Branch (nPC_sel, beq_out);  // OR_Gate
  buf ExtOp1 (ExtOp[1], lui_out);  // OR_Gate
  or ExtOp0 (ExtOp[0], lw_out, memset_out, sw_out);
  buf u_DMSrc (DMSrc, memset_out);  // OR_Gate
  or ALUOp1 (ALUOp[1], add_out, sub_out, sll_out, ssze_out, ori_out);
  buf ALUOp0 (ALUOp[0], ori_out);  // OR_Gate
  buf Jump1 (Jump[1], jr_out);  // OR_Gate
  buf Jump0 (Jump[0], jal_out);  // OR_Gate

  // Other names for the same wires on the sheet: F0 = in_2[0]; F1 = in_2[1]; F2 = in_2[2]; F3 = in_2[3]; F4 = in_2[4];
  //   F5 = in_2[5]
endmodule

module Ext (
  input  [1:0] ExtOp,
  input  [15:0] imm16,
  output [31:0] out_3
);

  wire [31:0] bit_extender_1_out, bit_extender_2_out;

  assign bit_extender_1_out = {{16{1'b0}}, imm16};  // Bit_Extender bit_extender_1
  assign bit_extender_2_out = {{16{imm16[15]}}, imm16};  // Bit_Extender bit_extender_2
  Multiplexer #(.select(2), .width(32), .enable("false")) multiplexer_1 (
    .in0(bit_extender_1_out), .in1(bit_extender_2_out), .in2({imm16, {16{1'b0}}}), .out(out_3), .sel(ExtOp));  // open: in3
endmodule

// DM
module DataMemory (
  input  [31:0] Address,
  input  [31:0] WD,
  input  MemWrite,
  input  clk,
  input  Reset,
  output [31:0] ReadData
);

  wire not_1_out;

  not not_1 (not_1_out, MemWrite);
  RAM #(.addrWidth(5), .dataWidth(32), .bus("separate")) ram_1 (
    .addr(Address[6:2]), .din(WD), .data(ReadData), .str(MemWrite), .clk(clk), .ld(not_1_out), .clr(Reset));  // open: sel
endmodule
